# Fritzing sketch Hardware (saved by Fritzing 0.9.9b)
breadboards: 1

parts:
  Raspberry_Pi_1 = Raspberry Pi 3 [part_number=RPI-3-V1.2]
  J1 = Basic Servo
  CAMERA1 = TTL Serial JPEG Camera  # not connected
  DRV_1 = DRV 8825 Stepper Motor Carrier, High Current [part_number="DRV 8825"]
  Power_plug1 = Power plug
  M3 = Stepper Motor - Bipolar  # not connected
  DRV_2 = DRV 8825 Stepper Motor Carrier, High Current [part_number="DRV 8825"]
  M4 = Stepper Motor - Bipolar  # not connected

nets:
  N1: Raspberry_Pi_1.GPIO2, DRV_1.STEP
  N2: Raspberry_Pi_1.GPIO3, DRV_1.DIRECTION
  GND: Raspberry_Pi_1.GND, J1.gnd, DRV_1.GROUND_LOG, DRV_2.GROUND_LOG
  N3: Raspberry_Pi_1.GIPO22, J1.pulse
  5V: Raspberry_Pi_1.5V, J1.vcc
  N4: Power_plug1.GND, DRV_2.VOLTAGE_ST/_MT
  N5: Power_plug1.VCC, DRV_2.GROUND_ST/_MT

custom parts:
  TTL Serial JPEG Camera: TTL Serial JPEG Camera with NTSC Out
